// Logisim project Calc_Logic.circ as structural Verilog: 19 circuits, main circuit main
module main (
  input  s4,
  input  s5,
  input  s3,
  input  s6,
  input  s2,
  input  s1,
  input  s0
);

  wire add_out, and_1_out, and_2_out, b0_out, b1_out, b2_out, b3_out, b4_out, b5_out, b6_out, b7_out, b8_out,
       b9_out, clock_1_out, clr_out, controller_1_clrs, controller_1_enables, controller_1_n_or_i,
       controller_1_val1_clr, controller_1_val1_en, d_ff_1_q, datapath_1_error, div_out, equals_out,
       mult_out, neg_out, not_1_out, not_2_out, not_3_out, not_4_out, num_enable_1_num_en,
       num_processor_1_eight_out, num_processor_1_five_out, num_processor_1_four_out,
       num_processor_1_nine_out, num_processor_1_one_out, num_processor_1_seven_out, num_processor_1_six_out,
       num_processor_1_three_out, num_processor_1_two_out, num_processor_1_zero_out, op_enable_1_op_en,
       op_processor_1_add_out, op_processor_1_clr_out, op_processor_1_div_out, op_processor_1_equals_out,
       op_processor_1_mult_out, op_processor_1_neg_out, op_processor_1_pwr_out, op_processor_1_sub_out,
       pwr_out, sub_out, undriven, valSelector_qn;
  wire [2:0] controller_1_n0, op_encoder_1_out_6, State_q;
  wire [3:0] num_encoder_1_out_11;
  wire [6:0] seven_seg_display_1_seg_0, seven_seg_display_1_seg_1, seven_seg_display_1_seg_2,
       seven_seg_display_1_seg_3, seven_seg_display_1_seg_4, seven_seg_display_1_seg_5,
       seven_seg_display_1_seg_6, seven_seg_display_1_seg_7, seven_seg_display_1_seg_8,
       seven_seg_display_1_seg_9;
  wire [31:0] datapath_1_numtodisplay;

  num_enable num_enable_1 (
    .num_0(num_processor_1_zero_out), .num_1(num_processor_1_one_out), .num_2(num_processor_1_two_out),
    .num_3(num_processor_1_three_out), .num_4(num_processor_1_four_out), .num_5(num_processor_1_five_out),
    .num_6(num_processor_1_six_out), .num_7(num_processor_1_seven_out), .num_8(num_processor_1_eight_out),
    .num_9(num_processor_1_nine_out), .num_en(num_enable_1_num_en));
  num_processor num_processor_1 (
    .clk(clock_1_out), .zero(b0_out), .one(b1_out), .two(b2_out), .three(b3_out), .four(b4_out),
    .five(b5_out), .six(b6_out), .seven(b7_out), .eight(b8_out), .nine(b9_out),
    .zero_out(num_processor_1_zero_out), .one_out(num_processor_1_one_out),
    .two_out(num_processor_1_two_out), .three_out(num_processor_1_three_out),
    .four_out(num_processor_1_four_out), .five_out(num_processor_1_five_out),
    .six_out(num_processor_1_six_out), .seven_out(num_processor_1_seven_out),
    .eight_out(num_processor_1_eight_out), .nine_out(num_processor_1_nine_out));
  Button b0 (.out(b0_out));
  Button b1 (.out(b1_out));
  Button b2 (.out(b2_out));
  Button b3 (.out(b3_out));
  Button b4 (.out(b4_out));
  Button b5 (.out(b5_out));
  Button b6 (.out(b6_out));
  Button b7 (.out(b7_out));
  not not_1 (not_1_out, State_q[2]);
  Button b8 (.out(b8_out));
  Button b9 (.out(b9_out));
  and and_1 (and_1_out, not_1_out, State_q[1], State_q[0]);
  not not_2 (not_2_out, State_q[1]);
  and and_2 (and_2_out, State_q[2], not_2_out, not_3_out);
  not not_3 (not_3_out, State_q[0]);
  op_enable op_enable_1 (
    .equals(op_processor_1_equals_out), .add(op_processor_1_add_out), .sub(op_processor_1_sub_out),
    .div(op_processor_1_div_out), .mult(op_processor_1_mult_out), .op_en(op_enable_1_op_en));
  op_processor op_processor_1 (
    .clk(clock_1_out), .pwr(pwr_out), .clr(clr_out), .neg(neg_out), .add(add_out), .subtract(sub_out),
    .divide(div_out), .multiply(mult_out), .equals(equals_out), .pwr_out(op_processor_1_pwr_out),
    .clr_out(op_processor_1_clr_out), .neg_out(op_processor_1_neg_out), .add_out(op_processor_1_add_out),
    .sub_out(op_processor_1_sub_out), .div_out(op_processor_1_div_out), .mult_out(op_processor_1_mult_out),
    .equals_out(op_processor_1_equals_out));
  Button pwr (.out(pwr_out));
  Button clr (.out(clr_out));
  Button neg (.out(neg_out));
  D_Flip_Flop valSelector (.Qn(valSelector_qn), .preset(and_1_out), .reset(and_2_out));  // open: D, clk, Q
  controller controller_1 (
    .s2(State_q[2]), .s1(State_q[1]), .s0(State_q[0]), .pwr(op_processor_1_pwr_out),
    .clr(op_processor_1_clr_out), .num(num_enable_1_num_en), .op(op_enable_1_op_en),
    .neg(op_processor_1_neg_out), .n_or_i(controller_1_n_or_i), .enables(controller_1_enables),
    .clrs(controller_1_clrs), .val1_en(controller_1_val1_en), .n2(controller_1_n0[2]),
    .n1(controller_1_n0[1]), .n0(controller_1_n0[0]), .val1_clr(controller_1_val1_clr));
  Button add (.out(add_out));
  Button sub (.out(sub_out));
  num_encoder num_encoder_1 (
    .n0(num_processor_1_zero_out), .n1(num_processor_1_one_out), .n2(num_processor_1_two_out),
    .n3(num_processor_1_three_out), .n4(num_processor_1_four_out), .n5(num_processor_1_five_out),
    .n6(num_processor_1_six_out), .n7(num_processor_1_seven_out), .n8(num_processor_1_eight_out),
    .n9(num_processor_1_nine_out), .out_11(num_encoder_1_out_11));
  op_encoder op_encoder_1 (
    .add(op_processor_1_add_out), .sub(op_processor_1_sub_out), .div(op_processor_1_div_out),
    .mult(op_processor_1_mult_out), .equals(op_processor_1_equals_out), .out_6(op_encoder_1_out_6));
  Button div (.out(div_out));
  _7_Segment_Display u_7_segment_display_1 (
    .g(seven_seg_display_1_seg_9[3]), .f(seven_seg_display_1_seg_9[4]), .a(seven_seg_display_1_seg_9[5]),
    .b(seven_seg_display_1_seg_9[6]), .e(seven_seg_display_1_seg_9[2]), .d(seven_seg_display_1_seg_9[1]),
    .c(seven_seg_display_1_seg_9[0]));  // open: dp
  Button mult (.out(mult_out));
  Register #(.width(3)) State (.D(controller_1_n0), .en(1'b1), .clk(clock_1_out), .Q(State_q));  // open: clr
  Clock clock_1 (.out(clock_1_out));
  not not_4 (not_4_out, clock_1_out);
  _7_Segment_Display u_7_segment_display_2 (
    .g(seven_seg_display_1_seg_8[3]), .f(seven_seg_display_1_seg_8[4]), .a(seven_seg_display_1_seg_8[5]),
    .b(seven_seg_display_1_seg_8[6]), .e(seven_seg_display_1_seg_8[2]), .d(seven_seg_display_1_seg_8[1]),
    .c(seven_seg_display_1_seg_8[0]));  // open: dp
  Button equals (.out(equals_out));
  _7_Segment_Display u_7_segment_display_3 (
    .g(seven_seg_display_1_seg_7[3]), .f(seven_seg_display_1_seg_7[4]), .a(seven_seg_display_1_seg_7[5]),
    .b(seven_seg_display_1_seg_7[6]), .e(seven_seg_display_1_seg_7[2]), .d(seven_seg_display_1_seg_7[1]),
    .c(seven_seg_display_1_seg_7[0]));  // open: dp
  datapath datapath_1 (
    .val1_en(controller_1_val1_en), .clr(controller_1_clrs), .enables(controller_1_enables),
    .n_or_i(controller_1_n_or_i), .valSelector(valSelector_qn), .num_val(num_encoder_1_out_11),
    .clk(not_4_out), .val1_clr(controller_1_val1_clr), .op_code(op_encoder_1_out_6),
    .NumToDisplay(datapath_1_numtodisplay), .Error(datapath_1_error));
  seven_seg_display seven_seg_display_1 (
    .in_1(datapath_1_numtodisplay), .seg_0(seven_seg_display_1_seg_0), .seg_1(seven_seg_display_1_seg_1),
    .seg_2(seven_seg_display_1_seg_2), .seg_3(seven_seg_display_1_seg_3), .seg_4(seven_seg_display_1_seg_4),
    .seg_5(seven_seg_display_1_seg_5), .seg_6(seven_seg_display_1_seg_6), .seg_7(seven_seg_display_1_seg_7),
    .seg_8(seven_seg_display_1_seg_8), .seg_9(seven_seg_display_1_seg_9));
  _7_Segment_Display u_7_segment_display_4 (
    .g(seven_seg_display_1_seg_6[3]), .f(seven_seg_display_1_seg_6[4]), .a(seven_seg_display_1_seg_6[5]),
    .b(seven_seg_display_1_seg_6[6]), .e(seven_seg_display_1_seg_6[2]), .d(seven_seg_display_1_seg_6[1]),
    .c(seven_seg_display_1_seg_6[0]));  // open: dp
  D_Flip_Flop d_ff_1 (.D(op_processor_1_clr_out), .clk(not_4_out), .Q(d_ff_1_q));  // open: Qn, preset, reset
  D_Flip_Flop d_ff_2 (.D(undriven), .preset(datapath_1_error), .reset(d_ff_1_q));  // open: clk, Q, Qn
  _7_Segment_Display u_7_segment_display_5 (
    .g(seven_seg_display_1_seg_5[3]), .f(seven_seg_display_1_seg_5[4]), .a(seven_seg_display_1_seg_5[5]),
    .b(seven_seg_display_1_seg_5[6]), .e(seven_seg_display_1_seg_5[2]), .d(seven_seg_display_1_seg_5[1]),
    .c(seven_seg_display_1_seg_5[0]));  // open: dp
  _7_Segment_Display u_7_segment_display_6 (
    .g(seven_seg_display_1_seg_4[3]), .f(seven_seg_display_1_seg_4[4]), .a(seven_seg_display_1_seg_4[5]),
    .b(seven_seg_display_1_seg_4[6]), .e(seven_seg_display_1_seg_4[2]), .d(seven_seg_display_1_seg_4[1]),
    .c(seven_seg_display_1_seg_4[0]));  // open: dp
  _7_Segment_Display u_7_segment_display_7 (.g(s3), .f(s4), .a(s5), .b(s6), .e(s2), .d(s1), .c(s0));  // open: dp
  _7_Segment_Display u_7_segment_display_8 (
    .g(seven_seg_display_1_seg_3[3]), .f(seven_seg_display_1_seg_3[4]), .a(seven_seg_display_1_seg_3[5]),
    .b(seven_seg_display_1_seg_3[6]), .e(seven_seg_display_1_seg_3[2]), .d(seven_seg_display_1_seg_3[1]),
    .c(seven_seg_display_1_seg_3[0]));  // open: dp
  _7_Segment_Display u_7_segment_display_9 (
    .g(seven_seg_display_1_seg_2[3]), .f(seven_seg_display_1_seg_2[4]), .a(seven_seg_display_1_seg_2[5]),
    .b(seven_seg_display_1_seg_2[6]), .e(seven_seg_display_1_seg_2[2]), .d(seven_seg_display_1_seg_2[1]),
    .c(seven_seg_display_1_seg_2[0]));  // open: dp
  _7_Segment_Display u_7_segment_display_10 (
    .g(seven_seg_display_1_seg_1[3]), .f(seven_seg_display_1_seg_1[4]), .a(seven_seg_display_1_seg_1[5]),
    .b(seven_seg_display_1_seg_1[6]), .e(seven_seg_display_1_seg_1[2]), .d(seven_seg_display_1_seg_1[1]),
    .c(seven_seg_display_1_seg_1[0]));  // open: dp
  _7_Segment_Display u_7_segment_display_11 (
    .g(seven_seg_display_1_seg_0[3]), .f(seven_seg_display_1_seg_0[4]), .a(seven_seg_display_1_seg_0[5]),
    .b(seven_seg_display_1_seg_0[6]), .e(seven_seg_display_1_seg_0[2]), .d(seven_seg_display_1_seg_0[1]),
    .c(seven_seg_display_1_seg_0[0]));  // open: dp
endmodule

module controller (
  input  s2,
  input  s1,
  input  s0,
  input  pwr,
  input  clr,
  input  num,
  input  op,
  input  neg,
  output n_or_i,
  output enables,
  output clrs,
  output val1_en,
  output n2,
  output n1,
  output n0,
  output val1_clr
);

  wire and_1_out, not_1_out, not_2_out, not_3_out, not_4_out, not_5_out, not_6_out, not_7_out, not_8_out,
       xor_1_out;

  not not_1 (not_1_out, s2);
  not not_2 (not_2_out, s1);
  not not_3 (not_3_out, s0);
  not not_4 (not_4_out, pwr);
  not not_5 (not_5_out, clr);
  not not_6 (not_6_out, num);
  not not_7 (not_7_out, op);
  and and_1 (and_1_out, s2, not_2_out, not_3_out);
  or or_1 (val1_clr, and_1_out, clrs);
  and and_2 (clrs, not_2_out, not_1_out);
  and and_3 (enables, not_3_out, not_2_out);
  xor xor_1 (xor_1_out, s1, s2);
  and and_4 (val1_en, s0, xor_1_out);
  n2_logic n2_logic_1 (
    .s2_not(not_1_out), .s1(s1), .s0_not(not_3_out), .pwr_not(not_4_out), .clr_not(not_5_out),
    .num_not(not_6_out), .op(op), .neg(neg), .n2_out(n2));
  not not_8 (not_8_out, neg);
  n1_logic n1_logic_1 (
    .s2(s2), .s1(s1), .s0(s0), .pwr_n(not_4_out), .clr_n(not_5_out), .num(num), .op_n(not_7_out),
    .neg_n(not_8_out), .n1_output(n1));
  n0_logic n0_logic_1 (
    .s2(s2), .s1(s1), .s0(s0), .pwr(pwr), .clr(clr), .num(num), .op_n(not_7_out), .neg(neg), .n0_clr(n0));

  assign n_or_i = s1;

  // Notes on the sheet:
  //   op_clr
  //   val1_clr
  //   val2_clr
  //   regs_clr
  //   val2_en
  //   eval_en
  //   opcode_en
endmodule

module n2_logic (
  input  s2_not,
  input  s1,
  input  s0_not,
  input  pwr_not,
  input  clr_not,
  input  num_not,
  input  op,
  input  neg,
  output n2_out
);

  wire and_1_out, and_2_out, and_3_out, and_4_out, and_5_out, and_6_out, not_1_out, or_1_out;

  and and_1 (and_1_out, s2_not, s1);
  not not_1 (not_1_out, op);
  and and_2 (and_2_out, and_1_out, s0_not);
  and and_3 (and_3_out, and_2_out, pwr_not);
  and and_4 (and_4_out, and_3_out, clr_not);
  and and_5 (and_5_out, not_1_out, neg);
  and and_6 (and_6_out, and_4_out, num_not);
  or or_1 (or_1_out, op, and_5_out);
  and and_7 (n2_out, and_6_out, or_1_out);
endmodule

module n1_logic (
  input  s2,
  input  s1,
  input  s0,
  input  pwr_n,
  input  clr_n,
  input  num,
  input  op_n,
  input  neg_n,
  output n1_output
);

  wire and_1_out, and_2_out, and_3_out, and_4_out, and_5_out, and_6_out, and_7_out, not_1_out, not_2_out,
       not_3_out, not_4_out, or_1_out, or_2_out, or_3_out;

  not not_1 (not_1_out, s2);
  not not_2 (not_2_out, s0);
  not not_3 (not_3_out, num);
  and and_1 (and_1_out, not_3_out, op_n);
  or or_1 (or_1_out, num, and_2_out);
  and and_2 (and_2_out, and_1_out, neg_n);
  and and_3 (and_3_out, not_2_out, or_1_out);
  not not_4 (not_4_out, s1);
  and and_4 (and_4_out, s1, and_3_out);
  or or_2 (or_2_out, s0, and_4_out);
  and and_5 (and_5_out, s2, not_4_out);
  and and_6 (and_6_out, not_1_out, or_2_out);
  and and_7 (and_7_out, pwr_n, clr_n);
  or or_3 (or_3_out, and_5_out, and_6_out);
  and and_8 (n1_output, and_7_out, or_3_out);
endmodule

module n0_logic (
  input  s2,
  input  s1,
  input  s0,
  input  pwr,
  input  clr,
  input  num,
  input  op_n,
  input  neg,
  output n0_clr
);

  wire and_1_out, and_2_out, and_3_out, and_4_out, and_5_out, and_6_out, and_7_out, and_8_out, and_9_out,
       and_10_out, and_11_out, and_12_out, and_13_out, not_1_out, not_2_out, not_3_out, not_4_out, not_5_out,
       not_6_out, or_1_out, or_2_out, or_3_out, or_4_out;

  not not_1 (not_1_out, s2);
  not not_2 (not_2_out, s1);
  not not_3 (not_3_out, s0);
  not not_4 (not_4_out, pwr);
  not not_5 (not_5_out, clr);
  not not_6 (not_6_out, num);
  and and_1 (and_1_out, not_6_out, op_n);
  or or_1 (or_1_out, num, and_2_out);
  and and_2 (and_2_out, and_1_out, neg);
  and and_3 (and_3_out, not_5_out, or_1_out);
  and and_4 (and_4_out, not_3_out, and_3_out);
  and and_5 (and_5_out, s0, clr);
  and and_6 (and_6_out, s1, or_2_out);
  or or_2 (or_2_out, clr, and_4_out);
  and and_7 (and_7_out, not_2_out, not_3_out);
  or or_3 (or_3_out, and_5_out, and_6_out);
  and and_8 (and_8_out, s2, not_2_out);
  and and_9 (and_9_out, and_7_out, pwr);
  and and_10 (and_10_out, not_4_out, or_3_out);
  and and_11 (and_11_out, and_8_out, not_4_out);
  or or_4 (or_4_out, and_9_out, and_10_out);
  and and_12 (and_12_out, and_11_out, clr);
  and and_13 (and_13_out, not_1_out, or_4_out);
  or or_5 (n0_clr, and_12_out, and_13_out);
endmodule

module number_decoder (
  input  [3:0] in_1,
  output num_0,
  output num_1,
  output num_2,
  output num_3,
  output num_4,
  output num_5,
  output num_6,
  output num_7,
  output num_8,
  output num_9
);

  wire and_1_out, and_2_out, and_3_out, and_4_out, and_5_out, and_6_out, and_7_out, and_8_out, and_9_out,
       and_10_out, and_11_out, and_12_out, and_13_out, and_14_out, and_15_out, and_16_out, and_17_out,
       and_18_out, and_19_out, and_20_out, not_1_out, not_2_out, not_3_out, not_4_out;

  not not_1 (not_1_out, in_1[0]);
  not not_2 (not_2_out, in_1[1]);
  not not_3 (not_3_out, in_1[2]);
  not not_4 (not_4_out, in_1[3]);
  and and_1 (and_1_out, not_1_out, not_2_out);
  and and_2 (and_2_out, in_1[0], not_2_out);
  and and_3 (and_3_out, not_1_out, in_1[1]);
  and and_4 (and_4_out, in_1[0], in_1[1]);
  and and_5 (and_5_out, not_1_out, not_2_out);
  and and_6 (and_6_out, in_1[0], not_2_out);
  and and_7 (and_7_out, not_1_out, in_1[1]);
  and and_8 (and_8_out, in_1[0], in_1[1]);
  and and_9 (and_9_out, not_1_out, not_2_out);
  and and_10 (and_10_out, in_1[0], not_2_out);
  and and_11 (and_11_out, and_1_out, not_3_out);
  and and_12 (and_12_out, and_2_out, not_3_out);
  and and_13 (and_13_out, and_3_out, not_3_out);
  and and_14 (and_14_out, and_4_out, not_3_out);
  and and_15 (and_15_out, and_5_out, in_1[2]);
  and and_16 (and_16_out, and_6_out, in_1[2]);
  and and_17 (and_17_out, and_7_out, in_1[2]);
  and and_18 (and_18_out, and_8_out, in_1[2]);
  and and_19 (and_19_out, and_9_out, not_3_out);
  and and_20 (and_20_out, and_10_out, not_3_out);
  and and_21 (num_0, and_11_out, not_4_out);
  and and_22 (num_1, and_12_out, not_4_out);
  and and_23 (num_2, and_13_out, not_4_out);
  and and_24 (num_3, and_14_out, not_4_out);
  and and_25 (num_4, and_15_out, not_4_out);
  and and_26 (num_5, and_16_out, not_4_out);
  and and_27 (num_6, and_17_out, not_4_out);
  and and_28 (num_7, and_18_out, not_4_out);
  and and_29 (num_8, and_19_out, in_1[3]);
  and and_30 (num_9, and_20_out, in_1[3]);
endmodule

module num_encoder (
  input  n0,
  input  n1,
  input  n2,
  input  n3,
  input  n4,
  input  n5,
  input  n6,
  input  n7,
  input  n8,
  input  n9,
  output [3:0] out_11
);

  wire and_1_out, and_2_out, and_3_out, and_4_out, and_5_out, and_6_out, and_7_out, and_8_out, and_9_out,
       and_10_out, and_12_out, and_13_out, and_14_out, and_15_out, and_16_out, and_17_out, and_18_out,
       and_19_out, and_20_out, not_3_out, not_4_out, not_5_out, not_6_out, not_7_out, not_8_out, not_9_out,
       not_10_out, or_1_out, or_2_out, or_4_out, or_5_out, or_6_out, or_7_out, or_8_out, or_10_out;

  and and_1 (and_1_out, n1, not_3_out);
  // NOT_Gate not_1 has open pins: in=n0, out=open
  and and_2 (and_2_out, and_1_out, not_4_out);
  or or_1 (or_1_out, and_2_out, n3);
  and and_3 (and_3_out, not_8_out, not_9_out);
  and and_4 (and_4_out, not_7_out, and_3_out);
  and and_5 (and_5_out, not_6_out, and_4_out);
  and and_6 (and_6_out, not_5_out, and_5_out);
  and and_7 (and_7_out, or_1_out, and_6_out);
  or or_2 (or_2_out, and_7_out, and_10_out);
  or or_3 (out_11[0], or_2_out, n9);
  // NOT_Gate not_2 has open pins: in=n1, out=open
  and and_8 (and_8_out, n5, not_7_out);
  and and_9 (and_9_out, and_8_out, not_8_out);
  or or_4 (or_4_out, and_9_out, n7);
  and and_10 (and_10_out, or_4_out, not_9_out);
  not not_3 (not_3_out, n2);
  xor xor_1 (out_11[3], n8, n9);
  not not_4 (not_4_out, n3);
  or or_5 (or_5_out, n4, n5);
  not not_5 (not_5_out, n4);
  or or_6 (or_6_out, or_5_out, n6);
  or or_7 (or_7_out, or_6_out, n7);
  and and_11 (out_11[2], or_7_out, and_12_out);
  not not_6 (not_6_out, n5);
  and and_12 (and_12_out, not_10_out, not_9_out);
  not not_7 (not_7_out, n6);
  and and_13 (and_13_out, not_7_out, and_19_out);
  and and_14 (and_14_out, not_6_out, and_13_out);
  or or_8 (or_8_out, n2, n3);
  and and_15 (and_15_out, not_5_out, and_14_out);
  and and_16 (and_16_out, or_8_out, and_15_out);
  and and_17 (and_17_out, or_10_out, and_20_out);
  or or_9 (out_11[1], and_16_out, and_17_out);
  not not_8 (not_8_out, n7);
  and and_18 (and_18_out, not_9_out, not_10_out);
  and and_19 (and_19_out, not_8_out, and_18_out);
  or or_10 (or_10_out, n6, n7);
  not not_9 (not_9_out, n8);
  and and_20 (and_20_out, not_9_out, not_9_out);
  not not_10 (not_10_out, n9);
endmodule

module op_encoder (
  input  add,
  input  sub,
  input  div,
  input  mult,
  input  equals,
  output [2:0] out_6
);

  wire and_1_out, and_2_out, and_3_out, and_5_out, not_1_out, not_2_out, not_3_out, not_4_out, or_1_out,
       or_2_out;

  not not_1 (not_1_out, sub);
  not not_2 (not_2_out, div);
  not not_3 (not_3_out, mult);
  not not_4 (not_4_out, equals);
  and and_1 (and_1_out, add, not_1_out);
  and and_2 (and_2_out, and_1_out, not_2_out);
  or or_1 (or_1_out, sub, div);
  and and_3 (and_3_out, not_3_out, not_4_out);
  or or_2 (or_2_out, and_2_out, div);
  and and_4 (out_6[1], or_1_out, and_3_out);
  and and_5 (and_5_out, or_2_out, not_3_out);
  or or_3 (out_6[0], and_5_out, equals);
  or or_4 (out_6[2], mult, equals);
endmodule

module op_decoder (
  input  b0,
  input  b1,
  input  b2,
  output add,
  output sub,
  output div,
  output mult
);

  wire and_1_out, and_2_out, and_3_out, and_4_out, not_1_out, not_2_out, not_3_out;

  not not_1 (not_1_out, b1);
  not not_2 (not_2_out, b2);
  not not_3 (not_3_out, b0);
  and and_1 (and_1_out, b0, not_1_out);
  and and_2 (and_2_out, b1, not_2_out);
  and and_3 (and_3_out, b1, not_2_out);
  and and_4 (and_4_out, b2, not_1_out);
  and and_5 (add, and_1_out, not_2_out);
  and and_6 (sub, and_2_out, not_3_out);
  and and_7 (div, and_3_out, b0);
  and and_8 (mult, and_4_out, not_3_out);
endmodule

module datapath (
  input  val1_en,
  input  clr,
  input  enables,
  input  n_or_i,
  input  valSelector,
  input  [3:0] num_val,
  input  clk,
  input  val1_clr,
  input  [2:0] op_code,
  output [31:0] NumToDisplay,
  output Error
);

  wire and_1_out, bitselector_1_out, bitselector_2_out, bitselector_3_out, comparator_1_gt, comparator_2_lt,
       d_ff_1_q, not_3_out, not_4_out, or_2_out, xnor_1_out, xor_1_out;
  wire [2:0] opcode_q;
  wire [31:0] adder_1_out, adder_2_out, adder_3_out, bit_extender_1_out, divider_1_out, multiplexer_1_out,
       multiplexer_2_out, multiplexer_3_out, multiplexer_4_out, multiplier_1_out, multiplier_2_out,
       not_1_out, not_2_out, not_5_out, value1_q, value2_q;

  assign bit_extender_1_out = {{28{1'b0}}, num_val};  // Bit_Extender bit_extender_1
  assign not_1_out = ~bit_extender_1_out;  // NOT_Gate not_1, 32 bits wide
  assign not_2_out = ~value1_q;  // NOT_Gate not_2, 32 bits wide
  D_Flip_Flop d_ff_1 (.D(val1_clr), .clk(not_3_out), .Q(d_ff_1_q));  // open: Qn, preset, reset
  not not_3 (not_3_out, clk);
  not not_4 (not_4_out, n_or_i);
  Adder #(.width(32)) adder_1 (.a(not_2_out), .b({32{1'b0}}), .out(adder_1_out), .cin(not_4_out));  // open: cout
  Multiplier #(.width(32)) multiplier_1 (
    .a(32'ha), .b(value1_q), .out(multiplier_1_out), .cin({32{1'b0}}));  // open: cout
  Multiplexer #(.width(32)) multiplexer_1 (
    .in0(bit_extender_1_out), .in1(not_1_out), .out(multiplexer_1_out), .sel(value1_q[31]));
  Adder #(.width(32)) adder_2 (
    .a(multiplier_1_out), .b(multiplexer_1_out), .out(adder_2_out), .cin(value1_q[31]));  // open: cout
  BitSelector #(.width(32)) bitselector_1 (.in(multiplier_1_out), .out(bitselector_1_out), .sel({5{1'b1}}));
  BitSelector #(.width(32)) bitselector_2 (.in(multiplexer_1_out), .out(bitselector_2_out), .sel({5{1'b1}}));
  xnor xnor_1 (xnor_1_out, bitselector_1_out, bitselector_2_out);
  Multiplexer #(.width(32)) multiplexer_2 (.in0(adder_1_out), .in1(adder_2_out), .out(multiplexer_2_out), .sel(n_or_i));
  BitSelector #(.width(32)) bitselector_3 (.in(adder_2_out), .out(bitselector_3_out), .sel({5{1'b1}}));
  and and_1 (and_1_out, xnor_1_out, n_or_i, xor_1_out);
  xor xor_1 (xor_1_out, bitselector_2_out, bitselector_3_out);
  Comparator #(.width(32)) comparator_1 (.a(value1_q), .b(32'h3b9ac9ff), .gt(comparator_1_gt));  // open: eq, lt
  or or_1 (Error, comparator_2_lt, or_2_out);
  or or_2 (or_2_out, comparator_1_gt, and_1_out);
  Comparator #(.width(32)) comparator_2 (.a(value1_q), .b(32'hc4653601), .lt(comparator_2_lt));  // open: gt, eq
  assign not_5_out = ~value1_q;  // NOT_Gate not_5, 32 bits wide
  Register #(.width(32)) value1 (.D(multiplexer_2_out), .en(val1_en), .clk(clk), .Q(value1_q), .clr(d_ff_1_q));
  Multiplexer #(.width(32)) multiplexer_3 (.in0(value1_q), .in1(not_5_out), .out(multiplexer_3_out), .sel(opcode_q[1]));
  Adder #(.width(32)) adder_3 (
    .a(value2_q), .b(multiplexer_3_out), .out(adder_3_out), .cin(opcode_q[1]));  // open: cout
  Divider #(.mode("twosComplement"), .width(32)) divider_1 (
    .a(value2_q), .b(value1_q), .out(divider_1_out));  // open: upper, rem
  Multiplier #(.mode("twosComplement"), .width(32)) multiplier_2 (
    .a(value2_q), .b(value1_q), .out(multiplier_2_out));  // open: cin, cout
  Multiplexer #(.select(3), .width(32)) multiplexer_4 (
    .in0(value1_q), .in1(adder_3_out), .in2(adder_3_out), .in3(divider_1_out), .in4(multiplier_2_out),
    .in5(value2_q), .in6({32{1'b0}}), .in7({32{1'b0}}), .out(multiplexer_4_out), .sel(opcode_q));
  Register #(.width(32)) value2 (.D(multiplexer_4_out), .en(enables), .clk(clk), .Q(value2_q), .clr(clr));
  Register #(.width(3)) opcode (.D(op_code), .en(enables), .clk(clk), .Q(opcode_q), .clr(clr));
  Multiplexer #(.width(32)) multiplexer_5 (.in0(value1_q), .in1(value2_q), .out(NumToDisplay), .sel(valSelector));

  // Notes on the sheet:
  //   sub_ctr
endmodule

module clear_reg (
  input  clr,
  output [31:0] out_2
);
endmodule

module num_enable (
  input  num_0,
  input  num_1,
  input  num_2,
  input  num_3,
  input  num_4,
  input  num_5,
  input  num_6,
  input  num_7,
  input  num_8,
  input  num_9,
  output num_en
);

  wire xor_1_out, xor_2_out, xor_3_out, xor_4_out, xor_5_out, xor_6_out, xor_7_out, xor_8_out;

  xor xor_1 (xor_1_out, num_0, num_1);
  xor xor_2 (xor_2_out, xor_1_out, num_2);
  xor xor_3 (xor_3_out, xor_2_out, num_3);
  xor xor_4 (xor_4_out, xor_3_out, num_4);
  xor xor_5 (xor_5_out, xor_4_out, num_5);
  xor xor_6 (xor_6_out, xor_5_out, num_6);
  xor xor_7 (xor_7_out, xor_6_out, num_7);
  xor xor_8 (xor_8_out, xor_7_out, num_8);
  xor xor_9 (num_en, xor_8_out, num_9);
endmodule

module op_enable (
  input  equals,
  input  add,
  input  sub,
  input  div,
  input  mult,
  output op_en
);

  wire xor_1_out, xor_2_out, xor_3_out;

  xor xor_1 (xor_1_out, equals, add);
  xor xor_2 (xor_2_out, xor_1_out, sub);
  xor xor_3 (xor_3_out, xor_2_out, div);
  xor xor_4 (op_en, xor_3_out, mult);
endmodule

module single_seg_encoder (
  input  b3,
  input  b2,
  input  b1,
  input  b0,
  output s0,
  output s1,
  output s2,
  output s3,
  output s4,
  output s5,
  output s6
);

  wire and_1_out, and_2_out, and_3_out, and_4_out, and_5_out, and_6_out, and_7_out, and_8_out, and_9_out,
       and_10_out, and_11_out, and_13_out, and_14_out, and_15_out, and_16_out, and_17_out, and_18_out,
       and_19_out, and_20_out, and_21_out, and_22_out, and_23_out, and_24_out, and_25_out, and_26_out,
       and_27_out, and_28_out, and_29_out, and_30_out, and_31_out, not_1_out, not_2_out, not_3_out,
       not_4_out, or_1_out, or_3_out, or_4_out, or_5_out, or_7_out, or_8_out, or_9_out, or_10_out, or_12_out,
       or_13_out, or_15_out, or_16_out, or_18_out, or_19_out;

  not not_1 (not_1_out, b3);
  not not_2 (not_2_out, b2);
  not not_3 (not_3_out, b1);
  not not_4 (not_4_out, b0);
  or or_1 (or_1_out, b2, b0);
  and and_1 (and_1_out, or_1_out, not_1_out);
  and and_2 (and_2_out, not_2_out, not_3_out);
  or or_2 (s0, and_1_out, and_2_out);
  or or_3 (or_3_out, not_4_out, b1);
  and and_3 (and_3_out, or_3_out, not_2_out);
  or or_4 (or_4_out, and_3_out, and_5_out);
  or or_5 (or_5_out, or_4_out, and_8_out);
  and and_4 (and_4_out, not_3_out, b2);
  and and_5 (and_5_out, b0, and_4_out);
  and and_6 (and_6_out, not_2_out, not_3_out);
  and and_7 (and_7_out, or_5_out, not_1_out);
  or or_6 (s1, and_7_out, and_9_out);
  and and_8 (and_8_out, b1, not_4_out);
  and and_9 (and_9_out, and_6_out, not_4_out);
  or or_7 (or_7_out, b1, not_2_out);
  and and_10 (and_10_out, or_7_out, not_1_out);
  and and_11 (and_11_out, not_2_out, not_3_out);
  or or_8 (or_8_out, and_10_out, and_11_out);
  and and_12 (s2, or_8_out, not_4_out);
  or or_9 (or_9_out, not_4_out, not_2_out);
  and and_13 (and_13_out, or_9_out, b1);
  or or_10 (or_10_out, and_13_out, and_14_out);
  and and_14 (and_14_out, b2, not_3_out);
  and and_15 (and_15_out, or_10_out, not_1_out);
  or or_11 (s3, and_15_out, and_17_out);
  and and_16 (and_16_out, not_2_out, b3);
  and and_17 (and_17_out, not_3_out, and_16_out);
  or or_12 (or_12_out, not_3_out, b2);
  and and_18 (and_18_out, or_12_out, not_4_out);
  and and_19 (and_19_out, b2, not_3_out);
  or or_13 (or_13_out, and_18_out, and_19_out);
  and and_20 (and_20_out, or_13_out, not_1_out);
  or or_14 (s4, and_20_out, and_22_out);
  and and_21 (and_21_out, not_2_out, not_3_out);
  and and_22 (and_22_out, b3, and_21_out);
  and and_23 (and_23_out, not_2_out, not_4_out);
  or or_15 (or_15_out, b1, and_23_out);
  or or_16 (or_16_out, or_15_out, and_25_out);
  and and_24 (and_24_out, or_16_out, not_1_out);
  and and_25 (and_25_out, b2, b0);
  and and_26 (and_26_out, not_2_out, not_3_out);
  and and_27 (and_27_out, b3, and_26_out);
  or or_17 (s5, and_24_out, and_27_out);
  or or_18 (or_18_out, not_3_out, not_2_out);
  and and_28 (and_28_out, or_18_out, not_4_out);
  and and_29 (and_29_out, b0, b1);
  or or_19 (or_19_out, and_28_out, and_29_out);
  and and_30 (and_30_out, or_19_out, not_1_out);
  or or_20 (s6, and_30_out, and_31_out);
  and and_31 (and_31_out, not_2_out, not_3_out);
endmodule

module button_processor (
  input  button,
  input  clk,
  output Y
);

  wire d_ff_1_q, d_ff_2_qn;

  D_Flip_Flop d_ff_1 (.D(button), .clk(clk), .Q(d_ff_1_q));  // open: Qn, preset, reset
  D_Flip_Flop d_ff_2 (.D(d_ff_1_q), .clk(clk), .Qn(d_ff_2_qn));  // open: Q, preset, reset
  and and_1 (Y, d_ff_2_qn, button);
endmodule

module num_processor (
  input  clk,
  input  zero,
  input  one,
  input  two,
  input  three,
  input  four,
  input  five,
  input  six,
  input  seven,
  input  eight,
  input  nine,
  output zero_out,
  output one_out,
  output two_out,
  output three_out,
  output four_out,
  output five_out,
  output six_out,
  output seven_out,
  output eight_out,
  output nine_out
);

  button_processor button_processor_1 (.button(zero), .clk(clk), .Y(zero_out));
  button_processor button_processor_2 (.button(one), .clk(clk), .Y(one_out));
  button_processor button_processor_3 (.button(two), .clk(clk), .Y(two_out));
  button_processor button_processor_4 (.button(three), .clk(clk), .Y(three_out));
  button_processor button_processor_5 (.button(four), .clk(clk), .Y(four_out));
  button_processor button_processor_6 (.button(five), .clk(clk), .Y(five_out));
  button_processor button_processor_7 (.button(six), .clk(clk), .Y(six_out));
  button_processor button_processor_8 (.button(seven), .clk(clk), .Y(seven_out));
  button_processor button_processor_9 (.button(eight), .clk(clk), .Y(eight_out));
  button_processor button_processor_10 (.button(nine), .clk(clk), .Y(nine_out));
endmodule

module op_processor (
  input  clk,
  input  pwr,
  input  clr,
  input  neg,
  input  add,
  input  subtract,
  input  divide,
  input  multiply,
  input  equals,
  output pwr_out,
  output clr_out,
  output neg_out,
  output add_out,
  output sub_out,
  output div_out,
  output mult_out,
  output equals_out
);

  wire d_ff_1_qn;

  D_Flip_Flop d_ff_1 (.D(pwr), .clk(clk), .Qn(d_ff_1_qn));  // open: Q, preset, reset
  and and_1 (pwr_out, pwr, d_ff_1_qn);
  button_processor button_processor_1 (.button(clr), .clk(clk), .Y(clr_out));
  button_processor button_processor_2 (.button(neg), .clk(clk), .Y(neg_out));
  button_processor button_processor_3 (.button(add), .clk(clk), .Y(add_out));
  button_processor button_processor_4 (.button(subtract), .clk(clk), .Y(sub_out));
  button_processor button_processor_5 (.button(divide), .clk(clk), .Y(div_out));
  button_processor button_processor_6 (.button(multiply), .clk(clk), .Y(mult_out));
  button_processor button_processor_7 (.button(equals), .clk(clk), .Y(equals_out));
endmodule

module seven_seg_display (
  input  [31:0] in_1,
  output [6:0] seg_0,
  output [6:0] seg_1,
  output [6:0] seg_2,
  output [6:0] seg_3,
  output [6:0] seg_4,
  output [6:0] seg_5,
  output [6:0] seg_6,
  output [6:0] seg_7,
  output [6:0] seg_8,
  output [6:0] seg_9
);

  wire [31:0] adder_1_out, adder_2_out, adder_3_out, adder_4_out, adder_5_out, adder_6_out, adder_7_out,
       adder_8_out, adder_9_out, divider_1_rem, divider_2_out, divider_3_out, divider_4_out, divider_5_out,
       divider_6_out, divider_7_out, divider_8_out, divider_9_out, divider_10_rem, divider_11_rem,
       divider_12_rem, divider_13_rem, divider_14_rem, divider_15_rem, divider_16_rem, divider_17_rem,
       multiplexer_1_out, multiplexer_2_out, multiplexer_3_out, multiplexer_4_out, multiplexer_5_out,
       multiplexer_6_out, multiplexer_7_out, multiplexer_8_out, multiplexer_9_out, not_1_out, not_2_out,
       not_3_out, not_4_out, not_5_out, not_6_out, not_7_out, not_8_out, not_9_out;

  assign not_1_out = ~in_1;  // NOT_Gate not_1, 32 bits wide
  Adder #(.width(32)) adder_1 (.a(not_1_out), .b({32{1'b0}}), .out(adder_1_out), .cin(in_1[31]));  // open: cout
  assign not_2_out = ~in_1;  // NOT_Gate not_2, 32 bits wide
  Adder #(.width(32)) adder_2 (.a(not_2_out), .b({32{1'b0}}), .out(adder_2_out), .cin(in_1[31]));  // open: cout
  assign not_3_out = ~in_1;  // NOT_Gate not_3, 32 bits wide
  assign not_4_out = ~in_1;  // NOT_Gate not_4, 32 bits wide
  assign not_5_out = ~in_1;  // NOT_Gate not_5, 32 bits wide
  assign not_6_out = ~in_1;  // NOT_Gate not_6, 32 bits wide
  assign not_7_out = ~in_1;  // NOT_Gate not_7, 32 bits wide
  assign not_8_out = ~in_1;  // NOT_Gate not_8, 32 bits wide
  assign not_9_out = ~in_1;  // NOT_Gate not_9, 32 bits wide
  Multiplexer #(.width(32)) multiplexer_1 (.in0(in_1), .in1(adder_1_out), .out(multiplexer_1_out), .sel(in_1[31]));
  Multiplexer #(.width(32)) multiplexer_2 (.in0(in_1), .in1(adder_2_out), .out(multiplexer_2_out), .sel(in_1[31]));
  Multiplexer #(.width(32)) multiplexer_3 (.in0(in_1), .in1(adder_3_out), .out(multiplexer_3_out), .sel(in_1[31]));
  Adder #(.width(32)) adder_3 (.a(not_3_out), .b({32{1'b0}}), .out(adder_3_out), .cin(in_1[31]));  // open: cout
  Multiplexer #(.width(32)) multiplexer_4 (.in0(in_1), .in1(adder_4_out), .out(multiplexer_4_out), .sel(in_1[31]));
  Adder #(.width(32)) adder_4 (.a(not_4_out), .b({32{1'b0}}), .out(adder_4_out), .cin(in_1[31]));  // open: cout
  Adder #(.width(32)) adder_5 (.a(not_5_out), .b({32{1'b0}}), .out(adder_5_out), .cin(in_1[31]));  // open: cout
  Adder #(.width(32)) adder_6 (.a(not_6_out), .b({32{1'b0}}), .out(adder_6_out), .cin(in_1[31]));  // open: cout
  Adder #(.width(32)) adder_7 (.a(not_7_out), .b({32{1'b0}}), .out(adder_7_out), .cin(in_1[31]));  // open: cout
  Adder #(.width(32)) adder_8 (.a(not_8_out), .b({32{1'b0}}), .out(adder_8_out), .cin(in_1[31]));  // open: cout
  Adder #(.width(32)) adder_9 (.a(not_9_out), .b({32{1'b0}}), .out(adder_9_out));  // open: cin, cout
  Multiplexer #(.width(32)) multiplexer_5 (.in0(in_1), .in1(adder_5_out), .out(multiplexer_5_out), .sel(in_1[31]));
  Multiplexer #(.width(32)) multiplexer_6 (.in0(in_1), .in1(adder_6_out), .out(multiplexer_6_out), .sel(in_1[31]));
  Multiplexer #(.width(32)) multiplexer_7 (.in0(in_1), .in1(adder_7_out), .out(multiplexer_7_out), .sel(in_1[31]));
  Multiplexer #(.width(32)) multiplexer_8 (.in0(in_1), .in1(adder_8_out), .out(multiplexer_8_out), .sel(in_1[31]));
  Multiplexer #(.width(32)) multiplexer_9 (.in0(in_1), .in1(adder_9_out), .out(multiplexer_9_out), .sel(in_1[31]));
  neg_encoder neg_encoder_1 (
    .sign_bit(in_1[31]), .s0(seg_9[0]), .s1(seg_9[1]), .s2(seg_9[2]), .s3(seg_9[3]), .s4(seg_9[4]),
    .s5(seg_9[5]), .s6(seg_9[6]));
  Divider #(.width(32)) divider_1 (.a(multiplexer_1_out), .b(32'ha), .rem(divider_1_rem));  // open: out, upper
  Divider #(.width(32)) divider_2 (.a(multiplexer_2_out), .b(32'ha), .out(divider_2_out));  // open: upper, rem
  Divider #(.width(32)) divider_3 (.a(multiplexer_3_out), .b(32'h64), .out(divider_3_out));  // open: upper, rem
  Divider #(.width(32)) divider_4 (.a(multiplexer_4_out), .b(32'h3e8), .out(divider_4_out));  // open: upper, rem
  Divider #(.width(32)) divider_5 (.a(multiplexer_5_out), .b(32'h2710), .out(divider_5_out));  // open: upper, rem
  Divider #(.width(32)) divider_6 (.a(multiplexer_6_out), .b(32'h186a0), .out(divider_6_out));  // open: upper, rem
  Divider #(.width(32)) divider_7 (.a(multiplexer_7_out), .b(32'hf4240), .out(divider_7_out));  // open: upper, rem
  Divider #(.width(32)) divider_8 (.a(multiplexer_8_out), .b(32'h989680), .out(divider_8_out));  // open: upper, rem
  Divider #(.width(32)) divider_9 (.a(multiplexer_9_out), .b(32'h5f5e100), .out(divider_9_out));  // open: upper, rem
  Divider #(.width(32)) divider_10 (.a(divider_2_out), .b(32'ha), .rem(divider_10_rem));  // open: out, upper
  Divider #(.width(32)) divider_11 (.a(divider_3_out), .b(32'ha), .rem(divider_11_rem));  // open: out, upper
  Divider #(.width(32)) divider_12 (.a(divider_4_out), .b(32'ha), .rem(divider_12_rem));  // open: out, upper
  Divider #(.width(32)) divider_13 (.a(divider_5_out), .b(32'ha), .rem(divider_13_rem));  // open: out, upper
  Divider #(.width(32)) divider_14 (.a(divider_6_out), .b(32'ha), .rem(divider_14_rem));  // open: out, upper
  Divider #(.width(32)) divider_15 (.a(divider_7_out), .b(32'ha), .rem(divider_15_rem));  // open: out, upper
  Divider #(.width(32)) divider_16 (.a(divider_8_out), .b(32'ha), .rem(divider_16_rem));  // open: out, upper
  Divider #(.width(32)) divider_17 (.a(divider_9_out), .b(32'ha), .rem(divider_17_rem));  // open: out, upper
  single_seg_encoder single_seg_encoder_1 (
    .b3(divider_1_rem[3]), .b2(divider_1_rem[2]), .b1(divider_1_rem[1]), .b0(divider_1_rem[0]),
    .s0(seg_0[0]), .s1(seg_0[1]), .s2(seg_0[2]), .s3(seg_0[3]), .s4(seg_0[4]), .s5(seg_0[5]), .s6(seg_0[6]));
  single_seg_encoder single_seg_encoder_2 (
    .b3(divider_10_rem[3]), .b2(divider_10_rem[2]), .b1(divider_10_rem[1]), .b0(divider_10_rem[0]),
    .s0(seg_1[0]), .s1(seg_1[1]), .s2(seg_1[2]), .s3(seg_1[3]), .s4(seg_1[4]), .s5(seg_1[5]), .s6(seg_1[6]));
  single_seg_encoder single_seg_encoder_3 (
    .b3(divider_11_rem[3]), .b2(divider_11_rem[2]), .b1(divider_11_rem[1]), .b0(divider_11_rem[0]),
    .s0(seg_2[0]), .s1(seg_2[1]), .s2(seg_2[2]), .s3(seg_2[3]), .s4(seg_2[4]), .s5(seg_2[5]), .s6(seg_2[6]));
  single_seg_encoder single_seg_encoder_4 (
    .b3(divider_12_rem[3]), .b2(divider_12_rem[2]), .b1(divider_12_rem[1]), .b0(divider_12_rem[0]),
    .s0(seg_3[0]), .s1(seg_3[1]), .s2(seg_3[2]), .s3(seg_3[3]), .s4(seg_3[4]), .s5(seg_3[5]), .s6(seg_3[6]));
  single_seg_encoder single_seg_encoder_5 (
    .b3(divider_13_rem[3]), .b2(divider_13_rem[2]), .b1(divider_13_rem[1]), .b0(divider_13_rem[0]),
    .s0(seg_4[0]), .s1(seg_4[1]), .s2(seg_4[2]), .s3(seg_4[3]), .s4(seg_4[4]), .s5(seg_4[5]), .s6(seg_4[6]));
  single_seg_encoder single_seg_encoder_6 (
    .b3(divider_14_rem[3]), .b2(divider_14_rem[2]), .b1(divider_14_rem[1]), .b0(divider_14_rem[0]),
    .s0(seg_5[0]), .s1(seg_5[1]), .s2(seg_5[2]), .s3(seg_5[3]), .s4(seg_5[4]), .s5(seg_5[5]), .s6(seg_5[6]));
  single_seg_encoder single_seg_encoder_7 (
    .b3(divider_15_rem[3]), .b2(divider_15_rem[2]), .b1(divider_15_rem[1]), .b0(divider_15_rem[0]),
    .s0(seg_6[0]), .s1(seg_6[1]), .s2(seg_6[2]), .s3(seg_6[3]), .s4(seg_6[4]), .s5(seg_6[5]), .s6(seg_6[6]));
  single_seg_encoder single_seg_encoder_8 (
    .b3(divider_16_rem[3]), .b2(divider_16_rem[2]), .b1(divider_16_rem[1]), .b0(divider_16_rem[0]),
    .s0(seg_7[0]), .s1(seg_7[1]), .s2(seg_7[2]), .s3(seg_7[3]), .s4(seg_7[4]), .s5(seg_7[5]), .s6(seg_7[6]));
  single_seg_encoder single_seg_encoder_9 (
    .b3(divider_17_rem[3]), .b2(divider_17_rem[2]), .b1(divider_17_rem[1]), .b0(divider_17_rem[0]),
    .s0(seg_8[0]), .s1(seg_8[1]), .s2(seg_8[2]), .s3(seg_8[3]), .s4(seg_8[4]), .s5(seg_8[5]), .s6(seg_8[6]));
endmodule

module neg_encoder (
  input  sign_bit,
  output s0,
  output s1,
  output s2,
  output s3,
  output s4,
  output s5,
  output s6
);

  wire not_1_out;

  not not_1 (not_1_out, sign_bit);
  and and_1 (s0, sign_bit, not_1_out);

  assign s1 = s0;
  assign s2 = s0;
  assign s3 = sign_bit;
  assign s4 = s0;
  assign s5 = s0;
  assign s6 = s0;
endmodule
